// Logisim project 8bitTo3dec.circ as structural Verilog: 1 circuit, main circuit main
module main (
  input  in_1,
  input  in_2,
  input  in_3,
  input  in_4,
  input  in_5,
  input  in_6,
  input  in_7,
  input  in_8
);

  wire c1_out_5, c1_out_6, c1_out_7, c1_out_8, c2_out_5, c2_out_6, c2_out_7, c2_out_8, c3_out_5, c3_out_6,
       c3_out_7, c3_out_8, c4_out_5, c4_out_6, c4_out_7, c4_out_8, c5_out_5, c5_out_6, c5_out_7, c5_out_8,
       c6_out_5, c6_out_6, c6_out_7, c6_out_8, c7_out_5, c7_out_6, c7_out_7, c7_out_8, not_1_out;

  // Probe on c6_out_5
  not not_1 (not_1_out, 1'b1);
  // Probe on c7_out_5
  bcd_decoder_main main_1 (
    .A(c7_out_5), .B(c6_out_5), .C(not_1_out), .D(not_1_out), .BLANKING(1'b1));  // open: a_2, b_2, c_2, d_2, e, f, g
  // Probe on c7_out_6
  shift3_display_main c6 (
    .in_1(1'b0), .in_2(c1_out_5), .in_3(c2_out_5), .in_4(c3_out_5), .out_5(c6_out_5), .out_6(c6_out_6),
    .out_7(c6_out_7), .out_8(c6_out_8));
  shift3_display_main c7 (
    .in_1(c6_out_6), .in_2(c6_out_7), .in_3(c6_out_8), .in_4(c4_out_5), .out_5(c7_out_5), .out_6(c7_out_6),
    .out_7(c7_out_7), .out_8(c7_out_8));
  // Probe on c7_out_7
  shift3_display_main c1 (
    .in_1(1'b0), .in_2(in_1), .in_3(in_2), .in_4(in_3), .out_5(c1_out_5), .out_6(c1_out_6), .out_7(c1_out_7),
    .out_8(c1_out_8));
  shift3_display_main c2 (
    .in_1(c1_out_6), .in_2(c1_out_7), .in_3(c1_out_8), .in_4(in_4), .out_5(c2_out_5), .out_6(c2_out_6),
    .out_7(c2_out_7), .out_8(c2_out_8));
  // Probe on c5_out_5
  // Probe on c7_out_8
  bcd_decoder_main main_2 (
    .A(c5_out_5), .B(c7_out_8), .C(c7_out_7), .D(c7_out_6), .BLANKING(1'b1));  // open: a_2, b_2, c_2, d_2, e, f, g
  shift3_display_main c3 (
    .in_1(c2_out_6), .in_2(c2_out_7), .in_3(c2_out_8), .in_4(in_5), .out_5(c3_out_5), .out_6(c3_out_6),
    .out_7(c3_out_7), .out_8(c3_out_8));
  // Probe on c5_out_6
  // Probe on c5_out_7
  shift3_display_main c4 (
    .in_1(c3_out_6), .in_2(c3_out_7), .in_3(c3_out_8), .in_4(in_6), .out_5(c4_out_5), .out_6(c4_out_6),
    .out_7(c4_out_7), .out_8(c4_out_8));
  shift3_display_main c5 (
    .in_1(c4_out_6), .in_2(c4_out_7), .in_3(c4_out_8), .in_4(in_7), .out_5(c5_out_5), .out_6(c5_out_6),
    .out_7(c5_out_7), .out_8(c5_out_8));
  // Probe on c5_out_8
  bcd_decoder_main main_3 (
    .A(in_8), .B(c5_out_8), .C(c5_out_7), .D(c5_out_6), .BLANKING(1'b1));  // open: a_2, b_2, c_2, d_2, e, f, g
  // Probe on in_8

  // Notes on the sheet:
  //   {           Huns           }
  //   {                              tens                }
  //   {                  Units               }
endmodule
