// Logisim project CPU.circ as structural Verilog: 1 circuit, main circuit main
module main (
  input  [7:0] Data_RAM,
  input  ON
);

  wire clock_1_out, CU_p3, CU_p4, CU_p6, CU_p7, CU_p8, CU_p9, CU_p10, CU_p11, CU_p12, CU_p13, not_1_out,
       not_2_out, not_3_out, not_4_out, not_5_out, not_6_out, or_3_out, or_4_out, or_5_out, or_6_out,
       or_7_out, or_8_out;
  wire [1:0] or_2_out;
  wire [3:0] CU_p2, IR_output, multiplexer_2_out, PC_out_5;
  wire [7:0] MBR_output, multiplexer_1_out, R1_output, R2_output;

  Clock #(.highDuration(3), .lowDuration(3)) clock_1 (.out(clock_1_out));
  or or_1 (or_2_out[1], CU_p7, not_2_out, not_1_out);
  not not_1 (not_1_out, CU_p8);
  not not_2 (not_2_out, CU_p9);
  Multiplexer #(.select(2), .width(8), .enable("false")) multiplexer_1 (
    .in0(R1_output), .in1(R2_output), .in2(Data_RAM), .out(multiplexer_1_out), .sel(or_2_out));  // open: in3
  or or_2 (or_2_out[0], not_4_out, CU_p9, not_3_out);
  not not_3 (not_3_out, CU_p8);
  not not_4 (not_4_out, CU_p7);
  or or_3 (or_3_out, CU_p8, CU_p6, CU_p9);
  Multiplexer #(.width(4), .enable("false")) multiplexer_2 (
    .in0(PC_out_5), .in1(IR_output), .out(multiplexer_2_out), .sel(not_5_out));
  not not_5 (not_5_out, CU_p3);
  or or_4 (or_4_out, CU_p3, CU_p7);
  _4_bit_register__MAR MAR (.Clock(clock_1_out), .R_0__W_1(or_4_out), .Input(multiplexer_2_out));  // open: Output
  Register MBR (.Clock(clock_1_out), .R_0__W_1(or_3_out), .Input(multiplexer_1_out), .Output(MBR_output));
  // CU CU: pin names not known; wires that end beside it: clock_1_out, CU_p2, CU_p3, CU_p4, ON, CU_p6, CU_p7, CU_p8, CU_p9, CU_p10, CU_p11, CU_p12, CU_p13
  Register IR (.Clock(clock_1_out), .R_0__W_1(CU_p4), .Input(MBR_output), .Output({CU_p2, IR_output}));
  or or_5 (or_5_out, CU_p12, CU_p13, CU_p3);
  or or_6 (or_6_out, CU_p13, CU_p12);
  programcounter__alec_main PC (
    .Clock(clock_1_out), .Activate(or_5_out), .INC_0__SET_1(or_6_out), .in_4(IR_output), .out_5(PC_out_5));
  Register R1 (.Clock(clock_1_out), .Output(R1_output));  // open: R_0__W_1, Input
  Register R2 (.Clock(clock_1_out), .Output(R2_output));  // open: R_0__W_1, Input
  not not_6 (not_6_out, CU_p10);
  or or_7 (or_7_out, not_6_out, CU_p11);
  or or_8 (or_8_out, CU_p10, CU_p11);
  alu_main ALU (
    .A(R1_output), .B(R2_output), .Control0(or_7_out), .Control1(or_8_out));  // open: Result, Zero, Carry, Overflow, Negative, are_equal
endmodule
