// Logisim project Control Unit.circ as structural Verilog: 15 circuits, main circuit Counter
module Counter (
  input  Clock,
  input  Start,
  output [15:0] out_3
);

  wire and_1_out, j_k_ff_2_qn, j_k_ff_3_qn, j_k_ff_4_qn;
  wire [3:0] j_k_ff_4_q;

  Decoder #(.select(4)) decoder_1 (
    .out0(out_3[15]), .out1(out_3[14]), .out2(out_3[13]), .out3(out_3[12]), .out4(out_3[11]),
    .out5(out_3[10]), .out6(out_3[9]), .out7(out_3[8]), .out8(out_3[7]), .out9(out_3[6]), .out10(out_3[5]),
    .out11(out_3[4]), .out12(out_3[3]), .out13(out_3[2]), .out14(out_3[1]), .out15(out_3[0]), .sel(j_k_ff_4_q));  // open: en
  J_K_Flip_Flop j_k_ff_1 (.J(1'b1), .clk(j_k_ff_2_qn), .K(1'b1), .Q(j_k_ff_4_q[3]));  // open: Qn, preset, en, reset
  J_K_Flip_Flop j_k_ff_2 (
    .J(1'b1), .clk(j_k_ff_3_qn), .K(1'b1), .Q(j_k_ff_4_q[2]), .Qn(j_k_ff_2_qn));  // open: preset, en, reset
  J_K_Flip_Flop j_k_ff_3 (
    .J(1'b1), .clk(j_k_ff_4_qn), .K(1'b1), .Q(j_k_ff_4_q[1]), .Qn(j_k_ff_3_qn));  // open: preset, en, reset
  J_K_Flip_Flop j_k_ff_4 (
    .J(1'b1), .clk(and_1_out), .K(1'b1), .Q(j_k_ff_4_q[0]), .Qn(j_k_ff_4_qn));  // open: preset, en, reset
  and and_1 (and_1_out, Clock, Start);
endmodule

module MBR____M_MAR (
  input  [3:0] OP,
  output out_2
);

  wire and_1_out, and_2_out, not_1_out, not_2_out, not_3_out, not_4_out;

  not not_1 (not_1_out, OP[1]);
  not not_2 (not_2_out, OP[3]);
  not not_3 (not_3_out, OP[2]);
  and and_1 (and_1_out, not_2_out, not_3_out, not_1_out, OP[0]);
  or or_1 (out_2, and_1_out, and_2_out);
  not not_4 (not_4_out, OP[0]);
  and and_2 (and_2_out, not_2_out, not_3_out, OP[1], not_4_out);
endmodule

module MAR____IR_address (
  input  [3:0] OP,
  output out_2
);

  wire and_1_out, and_2_out, and_3_out, and_4_out, not_1_out, not_2_out, not_3_out, not_4_out;

  not not_1 (not_1_out, OP[1]);
  not not_2 (not_2_out, OP[3]);
  not not_3 (not_3_out, OP[2]);
  and and_1 (and_1_out, not_2_out, not_3_out, not_1_out, OP[0]);
  not not_4 (not_4_out, OP[0]);
  and and_2 (and_2_out, not_2_out, not_3_out, OP[1], not_4_out);
  or or_1 (out_2, and_1_out, and_2_out, and_3_out, and_4_out);
  and and_3 (and_3_out, not_2_out, not_3_out, OP[1], OP[0]);
  and and_4 (and_4_out, not_2_out, OP[2], not_1_out, not_4_out);
endmodule

module MBR____R0 (
  input  [3:0] OP,
  output out_2
);

  wire not_1_out, not_2_out;

  not not_1 (not_1_out, OP[3]);
  not not_2 (not_2_out, OP[2]);
  and and_1 (out_2, not_1_out, not_2_out, OP[1], OP[0]);
endmodule

module MBR____R1 (
  input  [3:0] OP,
  output out_2
);

  wire not_1_out, not_2_out, not_3_out;

  not not_1 (not_1_out, OP[3]);
  not not_2 (not_2_out, OP[0]);
  not not_3 (not_3_out, OP[1]);
  and and_1 (out_2, not_1_out, OP[2], not_3_out, not_2_out);
endmodule

module M_MAR___MBR (
  input  [3:0] OP,
  output out_2
);

  wire and_1_out, and_2_out, not_1_out, not_2_out, not_3_out, not_4_out;

  not not_1 (not_1_out, OP[3]);
  not not_2 (not_2_out, OP[2]);
  and and_1 (and_1_out, not_1_out, not_2_out, OP[1], OP[0]);
  or or_1 (out_2, and_1_out, and_2_out);
  not not_3 (not_3_out, OP[0]);
  not not_4 (not_4_out, OP[0]);
  and and_2 (and_2_out, not_1_out, OP[2], not_4_out, not_3_out);
endmodule

module R0____MBR (
  input  [3:0] OP,
  output out_2
);

  wire not_1_out, not_2_out, not_3_out;

  not not_1 (not_1_out, OP[1]);
  not not_2 (not_2_out, OP[3]);
  not not_3 (not_3_out, OP[2]);
  and and_1 (out_2, not_2_out, not_3_out, not_1_out, OP[0]);
endmodule

module R1____MBR (
  input  [3:0] OP,
  output out_2
);

  wire not_1_out, not_2_out, not_3_out;

  not not_1 (not_1_out, OP[3]);
  not not_2 (not_2_out, OP[0]);
  not not_3 (not_3_out, OP[2]);
  and and_1 (out_2, not_1_out, not_3_out, OP[1], not_2_out);
endmodule

module A_B_alu____registers (
  input  [3:0] OP,
  output out_2
);

  wire and_1_out, and_2_out, and_3_out, and_4_out, not_1_out, not_2_out, not_3_out, not_4_out;

  not not_1 (not_1_out, OP[1]);
  not not_2 (not_2_out, OP[3]);
  and and_1 (and_1_out, not_2_out, OP[2], not_1_out, OP[0]);
  not not_3 (not_3_out, OP[0]);
  and and_2 (and_2_out, not_2_out, OP[2], OP[1], not_3_out);
  or or_1 (out_2, and_1_out, and_2_out, and_4_out, and_3_out);
  not not_4 (not_4_out, OP[2]);
  and and_3 (and_3_out, OP[3], not_4_out, not_1_out, not_3_out);
  and and_4 (and_4_out, not_2_out, OP[2], OP[1], OP[0]);
endmodule

module Add_ALU (
  input  [3:0] OP,
  output out_2
);

  wire not_1_out, not_2_out;

  not not_1 (not_1_out, OP[1]);
  not not_2 (not_2_out, OP[3]);
  and and_1 (out_2, not_2_out, OP[2], not_1_out, OP[0]);
endmodule

module SUB_ALU (
  input  [3:0] OP,
  output out_2
);

  wire not_1_out, not_2_out;

  not not_1 (not_1_out, OP[0]);
  not not_2 (not_2_out, OP[3]);
  and and_1 (out_2, not_2_out, OP[2], OP[1], not_1_out);
endmodule

module Compare_ALU (
  input  [3:0] OP,
  output out_2
);

  wire and_1_out, and_2_out, not_1_out, not_2_out, not_3_out, not_4_out;

  not not_1 (not_1_out, OP[3]);
  and and_1 (and_1_out, not_1_out, OP[2], OP[1], OP[0]);
  or or_1 (out_2, and_1_out, and_2_out);
  not not_2 (not_2_out, OP[0]);
  not not_3 (not_3_out, OP[2]);
  not not_4 (not_4_out, OP[1]);
  and and_2 (and_2_out, OP[3], not_3_out, not_4_out, not_2_out, not_2_out);
endmodule

module PC____IR_Address____br_eq (
  input  [3:0] OP,
  output out_2
);

  wire not_1_out;

  not not_1 (not_1_out, OP[3]);
  and and_1 (out_2, not_1_out, OP[2], OP[1], OP[0]);
endmodule

module PC____IR_Address____br_n_eq (
  input  [3:0] OP,
  output out_2
);

  wire not_1_out, not_2_out, not_3_out;

  not not_1 (not_1_out, OP[1]);
  not not_2 (not_2_out, OP[2]);
  not not_3 (not_3_out, OP[0]);
  and and_1 (out_2, OP[3], not_2_out, not_1_out, not_3_out);
endmodule

module CU (
  input  Start,
  input  [3:0] OP_code,
  output MBR__M_MAR,
  output MAR____IR_address,
  output MBR____R0,
  output MBR____R1,
  output ADD_alu,
  output Substract_alu,
  output Compare_alu,
  output A_B_alu_____registers,
  output PC__IR_address____br_eq,
  output PC__IR_address____br_n_eq,
  output MAR__Pc__PC_plus_plus,
  output IR__MBR
);

  wire a_b_alu_registers_1_out_2, add_alu_1_out_2, and_1_out, clock_1_out, compare_alu_1_out_2,
       MAR__IR_address_out_2, MBR__M_MAR_out_2, mbr_r0_1_out_2, mbr_r1_1_out_2, pc_ir_address_br_eq_1_out_2,
       pc_ir_address_br_n_eq_1_out_2, sub_alu_1_out_2;
  wire [15:0] counter_1_out_3;

  MBR____M_MAR u_MBR__M_MAR (.OP(OP_code), .out_2(MBR__M_MAR_out_2));
  MAR____IR_address MAR__IR_address (.OP(OP_code), .out_2(MAR__IR_address_out_2));
  MBR____R0 mbr_r0_1 (.OP(OP_code), .out_2(mbr_r0_1_out_2));
  MBR____R1 mbr_r1_1 (.OP(OP_code), .out_2(mbr_r1_1_out_2));
  M_MAR___MBR m_mar_mbr_1 (.OP(OP_code));  // open: out_2
  R0____MBR r0_mbr_1 (.OP(OP_code));  // open: out_2
  R1____MBR r1_mbr_1 (.OP(OP_code));  // open: out_2
  A_B_alu____registers a_b_alu_registers_1 (.OP(OP_code), .out_2(a_b_alu_registers_1_out_2));
  Add_ALU add_alu_1 (.OP(OP_code), .out_2(add_alu_1_out_2));
  SUB_ALU sub_alu_1 (.OP(OP_code), .out_2(sub_alu_1_out_2));
  Compare_ALU compare_alu_1 (.OP(OP_code), .out_2(compare_alu_1_out_2));
  PC____IR_Address____br_eq pc_ir_address_br_eq_1 (.OP(OP_code), .out_2(pc_ir_address_br_eq_1_out_2));
  PC____IR_Address____br_n_eq pc_ir_address_br_n_eq_1 (.OP(OP_code), .out_2(pc_ir_address_br_n_eq_1_out_2));
  Clock clock_1 (.out(clock_1_out));
  Counter counter_1 (
    .out_3({counter_1_out_3[15], MAR__Pc__PC_plus_plus, counter_1_out_3[13], IR__MBR, counter_1_out_3[11:0]}),
    .Clock(clock_1_out), .Start(Start));
  and and_1 (and_1_out, counter_1_out_3[10], MBR__M_MAR_out_2);
  and and_2 (MAR____IR_address, counter_1_out_3[11], MAR__IR_address_out_2);
  and and_3 (MBR____R0, counter_1_out_3[10], mbr_r0_1_out_2);
  and and_4 (MBR____R1, counter_1_out_3[10], mbr_r1_1_out_2);
  and and_5 (ADD_alu, counter_1_out_3[10], add_alu_1_out_2);
  and and_6 (Substract_alu, counter_1_out_3[10], sub_alu_1_out_2);
  and and_7 (Compare_alu, counter_1_out_3[10], compare_alu_1_out_2);
  and and_8 (A_B_alu_____registers, a_b_alu_registers_1_out_2, counter_1_out_3[11]);
  and and_9 (PC__IR_address____br_eq, counter_1_out_3[9], pc_ir_address_br_eq_1_out_2);
  and and_10 (PC__IR_address____br_n_eq, counter_1_out_3[9], pc_ir_address_br_n_eq_1_out_2);
  or or_1 (MBR__M_MAR, counter_1_out_3[13], and_1_out);
endmodule
