// Logisim project PC & Incrementer.circ as structural Verilog: 1 circuit, main circuit 4-bit PC & incrementer
module _4_bit_PC___incrementer (
  input  Increment,
  output [3:0] out_2
);

  wire j_k_ff_2_qn, j_k_ff_3_qn, j_k_ff_4_qn;

  J_K_Flip_Flop j_k_ff_1 (.J(1'b1), .clk(j_k_ff_2_qn), .K(1'b1), .Q(out_2[3]));  // open: Qn, preset, en, reset
  J_K_Flip_Flop j_k_ff_2 (
    .J(1'b1), .clk(j_k_ff_3_qn), .K(1'b1), .Q(out_2[2]), .Qn(j_k_ff_2_qn));  // open: preset, en, reset
  J_K_Flip_Flop j_k_ff_3 (
    .J(1'b1), .clk(j_k_ff_4_qn), .K(1'b1), .Q(out_2[1]), .Qn(j_k_ff_3_qn));  // open: preset, en, reset
  J_K_Flip_Flop j_k_ff_4 (
    .J(1'b1), .clk(Increment), .K(1'b1), .Q(out_2[0]), .Qn(j_k_ff_4_qn));  // open: preset, en, reset
endmodule
