// Logisim project SystemSide_Draft.circ as structural Verilog: 1 circuit, main circuit main
module main (
  input  ON,
  output [7:0] out_2
);

  wire _0_out, _1_out, _2_out, _3_out, _4_out, _5_out, _6_out, _7_out, _8_out, _9_out, ALU_are_equal,
       and_1_out, and_2_out, and_3_out, and_4_out, and_5_out, and_6_out, and_7_out, clock_1_out,
       CU_a_b_alu_____registers, CU_add_alu, CU_display____ram_1111, CU_ir__mbr, CU_m_mar_____mbr,
       CU_mar____ir_address, CU_mar__pc__pc_plus_plus, CU_mbr____ram_1111, CU_mbr__m_mar,
       CU_pc__ir_address____br_eq, CU_pc__ir_address____br_n_eq, CU_r0____mbr, CU_r1____mbr,
       CU_ram_1111_____mbr, CU_substract_alu, main_1_out_2, main_1_out_3, main_1_out_4, main_1_out_5,
       main_1_out_6, main_1_out_7, main_1_out_8, main_1_out_9, main_1_out_10, main_1_out_11, main_1_out_12,
       main_1_out_13, main_1_out_14, main_1_out_15, main_1_out_16, main_1_out_17, main_1_out_18,
       main_1_out_19, main_1_out_20, main_1_out_21, main_1_out_22, not_1_out, not_2_out, not_3_out,
       not_4_out, or_3_out, or_4_out, or_5_out, or_6_out, or_7_out, or_8_out, or_9_out, or_10_out, ram_1_p1;
  wire [1:0] CU_mbr____r0, CU_r1____alu_result, or_1_out;
  wire [3:0] IR_output, main_3_out_5, MAR_output, multiplexer_5_out, ram_1_p5;
  wire [7:0] ALU_result, keypadblackbox_1_out_11, L_output, main_2_p3, MBR_output, multiplexer_4_out,
       multiplexer_6_out, multiplexer_7_out, multiplexer_8_out, multiplexer_9_out, R0_output, R1_output,
       R_output, ram_1_p13, ram_1_p22;
  wire [7:4] IR_output_2;

  Clock clock_1 (.out(clock_1_out));
  _7_Segment_Display u_7_segment_display_1 (
    .g(main_1_out_17), .f(main_1_out_18), .a(main_1_out_2), .b(main_1_out_5), .e(main_1_out_14),
    .d(main_1_out_11), .c(main_1_out_8));  // open: dp
  Button _1 (.out(_1_out));
  Button _4 (.out(_4_out));
  Button _7 (.out(_7_out));
  _7_Segment_Display u_7_segment_display_2 (
    .g(main_1_out_19), .f(main_1_out_20), .a(main_1_out_3), .b(main_1_out_6), .e(main_1_out_15),
    .d(main_1_out_12), .c(main_1_out_9));  // open: dp
  // RAM ram_1: pin names not known; wires that end beside it: ram_1_p1, ram_1_p5[3], ram_1_p5[2], ram_1_p5[1], ram_1_p5[0], ram_1_p13[7], ram_1_p13[6], ram_1_p13[5], ram_1_p13[4], ram_1_p13[3], ram_1_p13[2], ram_1_p13[1], ram_1_p13[0], clock_1_out, ram_1_p22[7], ram_1_p22[6], ram_1_p22[5], ram_1_p22[4], ram_1_p22[3], ram_1_p22[2], ram_1_p22[1], ram_1_p22[0]
  Multiplexer #(.width(8), .enable("false")) multiplexer_1 (
    .in0(out_2), .in1(keypadblackbox_1_out_11), .out(ram_1_p13), .sel(or_1_out[1]));
  Button _2 (.out(_2_out));
  Button _5 (.out(_5_out));
  Button _8 (.out(_8_out));
  Button _0 (.out(_0_out));
  Button _3 (.out(_3_out));
  Button _6 (.out(_6_out));
  Button _9 (.out(_9_out));
  keypadblackbox keypadblackbox_1 (
    .in_1(_0_out), .in_2(_1_out), .in_3(_2_out), .in_4(_3_out), .in_5(_4_out), .in_6(_5_out), .in_7(_6_out),
    .in_8(_7_out), .in_9(_8_out), .in_10(_9_out), .out_11(keypadblackbox_1_out_11));
  _7_Segment_Display u_7_segment_display_3 (
    .g(main_1_out_21), .f(main_1_out_22), .a(main_1_out_4), .b(main_1_out_7), .e(main_1_out_16),
    .d(main_1_out_13), .c(main_1_out_10));  // open: dp
  // Probe on ram_1_p5
  _8bitTo3dec_main main_1 (
    .out_19(main_1_out_19), .out_20(main_1_out_20), .out_15(main_1_out_15), .out_9(main_1_out_9),
    .out_12(main_1_out_12), .out_6(main_1_out_6), .out_3(main_1_out_3), .out_4(main_1_out_4),
    .out_7(main_1_out_7), .out_10(main_1_out_10), .out_13(main_1_out_13), .out_16(main_1_out_16),
    .out_21(main_1_out_21), .out_22(main_1_out_22), .out_2(main_1_out_2), .out_5(main_1_out_5),
    .out_8(main_1_out_8), .out_11(main_1_out_11), .out_14(main_1_out_14), .out_17(main_1_out_17),
    .out_18(main_1_out_18), .in_1(out_2));
  Multiplexer #(.select(2), .width(8), .enable("false")) multiplexer_2 (
    .in0(ram_1_p22), .in1(MBR_output), .in2(keypadblackbox_1_out_11), .out(out_2), .sel(or_1_out));  // open: in3
  or or_1 (or_1_out[0], CU_ram_1111_____mbr, CU_m_mar_____mbr);
  // Probe on MBR_output
  Multiplexer #(.width(4), .enable("false")) multiplexer_3 (
    .in0(MAR_output), .in1(4'b1111), .out(ram_1_p5), .sel(or_10_out));
  or or_2 (ram_1_p1, or_1_out[1], CU_ram_1111_____mbr, CU_m_mar_____mbr, CU_display____ram_1111);
  Multiplexer #(.select(2), .width(8), .enable("false")) multiplexer_4 (
    .in0(out_2), .in1(R0_output), .in2(R1_output), .out(multiplexer_4_out), .sel(CU_mbr____r0));  // open: in3
  Multiplexer #(.width(4), .enable("false")) multiplexer_5 (
    .in0(main_3_out_5), .in1(IR_output), .out(multiplexer_5_out), .sel(CU_mar____ir_address));
  not not_1 (not_1_out, IR_output[0]);
  Multiplexer #(.select(2), .width(8), .enable("false")) multiplexer_6 (
    .in0(MBR_output), .in1(ALU_result), .in3(main_2_p3), .out(multiplexer_6_out), .sel(CU_r1____alu_result));  // open: in2
  Multiplexer #(.select(2), .width(8), .enable("false")) multiplexer_7 (
    .in0(MBR_output), .in1(ALU_result), .in2(main_2_p3), .out(multiplexer_7_out), .sel(CU_r1____alu_result));  // open: in3
  or or_3 (or_3_out, CU_mbr____ram_1111, CU_mbr____r0[1], CU_mbr____r0[0], CU_mbr__m_mar);
  and and_1 (and_1_out, not_1_out, CU_r1____alu_result[0]);
  and and_2 (and_2_out, IR_output[0], CU_r1____alu_result[0]);
  and and_3 (and_3_out, IR_output[0], CU_r1____alu_result[1]);
  not not_2 (not_2_out, IR_output[0]);
  and and_4 (and_4_out, not_2_out, CU_r1____alu_result[1]);
  _4_bit_register__MAR MAR (.Clock(clock_1_out), .R_0__W_1(or_4_out), .Input(multiplexer_5_out), .Output(MAR_output));
  or or_4 (or_4_out, CU_mar__pc__pc_plus_plus, CU_mar____ir_address);
  Register MBR (.Clock(clock_1_out), .R_0__W_1(or_3_out), .Input(multiplexer_4_out), .Output(MBR_output));
  Register R0 (.Clock(clock_1_out), .R_0__W_1(or_5_out), .Input(multiplexer_6_out), .Output(R0_output));
  or or_5 (or_5_out, CU_r0____mbr, and_1_out, and_3_out);
  or or_6 (or_6_out, and_4_out, and_2_out, CU_r1____mbr);
  Register R1 (.Clock(clock_1_out), .R_0__W_1(or_6_out), .Input(multiplexer_7_out), .Output(R1_output));
  and and_5 (and_5_out, clock_1_out, CU_ir__mbr);
  // multiply_main main_2: pin names not known; wires that end beside it: R0_output, R1_output, main_2_p3
  // Probe on main_3_out_5
  programcounter__alec_main main_3 (
    .Clock(clock_1_out), .Activate(and_5_out), .INC_0__SET_1(or_8_out), .in_4(IR_output), .out_5(main_3_out_5));
  Multiplexer #(.width(8), .enable("false")) multiplexer_8 (
    .in0(R0_output), .in1(R1_output), .out(multiplexer_8_out), .sel(IR_output[1]));
  Multiplexer #(.width(8), .enable("false")) multiplexer_9 (
    .in0(R0_output), .in1(R1_output), .out(multiplexer_9_out), .sel(IR_output[2]));
  Register IR (.Clock(clock_1_out), .R_0__W_1(CU_ir__mbr), .Input(MBR_output), .Output({IR_output_2, IR_output}));
  or or_7 (or_7_out, not_3_out, CU_substract_alu);
  Register L (.Clock(clock_1_out), .R_0__W_1(CU_a_b_alu_____registers), .Input(multiplexer_8_out), .Output(L_output));
  Register R (.Clock(clock_1_out), .R_0__W_1(CU_a_b_alu_____registers), .Input(multiplexer_9_out), .Output(R_output));
  alu_main ALU (
    .A(L_output), .B(R_output), .Result(ALU_result), .Add_0_Sub_1(or_7_out), .Logic_0_Math_1(or_9_out),
    .are_equal(ALU_are_equal));  // open: Zero, Carry, Overflow, Negative
  and and_6 (and_6_out, CU_pc__ir_address____br_n_eq, not_4_out);
  or or_8 (or_8_out, and_6_out, and_7_out);
  not not_3 (not_3_out, CU_add_alu);
  or or_9 (or_9_out, CU_add_alu, CU_substract_alu);
  not not_4 (not_4_out, ALU_are_equal);
  and and_7 (and_7_out, ALU_are_equal, CU_pc__ir_address____br_eq);
  CU CU (
    .Clock(clock_1_out), .OP_code(IR_output_2), .Start(ON), .MAR__Pc__PC_plus_plus(CU_mar__pc__pc_plus_plus),
    .IR__MBR(CU_ir__mbr), .MBR__M_MAR(CU_mbr__m_mar), .MAR____IR_address(CU_mar____ir_address),
    .MBR____R0(CU_mbr____r0[0]), .MBR____R1(CU_mbr____r0[1]), .M_MAR_____MBR(CU_m_mar_____mbr),
    .ADD_alu(CU_add_alu), .Substract_alu(CU_substract_alu), .R0____MBR(CU_r0____mbr),
    .R1____MBR(CU_r1____mbr), .A_B_alu_____registers(CU_a_b_alu_____registers),
    .R1____ALU_result(CU_r1____alu_result[0]), .PC__IR_address____br_eq(CU_pc__ir_address____br_eq),
    .PC__IR_address____br_n_eq(CU_pc__ir_address____br_n_eq), .RAM_1111_____MBR(CU_ram_1111_____mbr),
    .Display____RAM_1111(CU_display____ram_1111), .RAM_1111_____Display(or_1_out[1]),
    .MBR____RAM_1111(CU_mbr____ram_1111), .Multiply(CU_r1____alu_result[1]));  // open: R____Multiply_result
  or or_10 (or_10_out, CU_mbr____ram_1111, or_1_out[1], CU_display____ram_1111, CU_ram_1111_____mbr);

  // Notes on the sheet:
  //   RAM(0)/MBR(1)/Keypad(2) to bus
  //   data 8-bit
  //   Address
  //   r(0)/w(1)
  //   MBR(0)/Keypad(1) to RAM
endmodule
