// Logisim project programcounter__alec.circ as structural Verilog: 1 circuit, main circuit main
module main (
  input  Clock,
  input  Activate,
  input  INC_0__SET_1,
  input  [3:0] in_4,
  output [3:0] out_5
);

  wire and_1_out, d_ff_1_qn, d_ff_2_qn, d_ff_3_qn, d_ff_4_qn, multiplexer_1_out, multiplexer_2_out,
       multiplexer_3_out, multiplexer_4_out, multiplexer_5_out, multiplexer_6_out, multiplexer_7_out;

  and and_1 (and_1_out, Clock, Activate);
  Multiplexer #(.enable("false")) multiplexer_1 (
    .in0(d_ff_1_qn), .in1(in_4[0]), .out(multiplexer_1_out), .sel(INC_0__SET_1));
  D_Flip_Flop d_ff_1 (.clk(and_1_out), .D(multiplexer_1_out), .Q(out_5[0]), .Qn(d_ff_1_qn));  // open: preset, en, reset
  Multiplexer #(.enable("false")) multiplexer_2 (
    .in0(d_ff_1_qn), .in1(and_1_out), .out(multiplexer_2_out), .sel(INC_0__SET_1));
  Multiplexer #(.enable("false")) multiplexer_3 (
    .in0(d_ff_2_qn), .in1(in_4[1]), .out(multiplexer_3_out), .sel(INC_0__SET_1));
  D_Flip_Flop d_ff_2 (
    .clk(multiplexer_2_out), .D(multiplexer_3_out), .Q(out_5[1]), .Qn(d_ff_2_qn));  // open: preset, en, reset
  Multiplexer #(.enable("false")) multiplexer_4 (
    .in0(d_ff_2_qn), .in1(and_1_out), .out(multiplexer_4_out), .sel(INC_0__SET_1));
  Multiplexer #(.enable("false")) multiplexer_5 (
    .in0(d_ff_3_qn), .in1(in_4[2]), .out(multiplexer_5_out), .sel(INC_0__SET_1));
  D_Flip_Flop d_ff_3 (
    .clk(multiplexer_4_out), .D(multiplexer_5_out), .Q(out_5[2]), .Qn(d_ff_3_qn));  // open: preset, en, reset
  Multiplexer #(.enable("false")) multiplexer_6 (
    .in0(d_ff_3_qn), .in1(multiplexer_4_out), .out(multiplexer_6_out), .sel(INC_0__SET_1));
  Multiplexer #(.enable("false")) multiplexer_7 (
    .in0(d_ff_4_qn), .in1(in_4[3]), .out(multiplexer_7_out), .sel(INC_0__SET_1));
  D_Flip_Flop d_ff_4 (
    .clk(multiplexer_6_out), .D(multiplexer_7_out), .Q(out_5[3]), .Qn(d_ff_4_qn));  // open: preset, en, reset
endmodule
